# Fritzing sketch exjobb (saved by Fritzing 0.9.3b)
breadboards: 1

parts:
  Raspberry_Pi_1 = Raspberry Pi 4 [part_number=RPI-4-b]
  Part1 = Thumb Joystick
  IC1 = MCP3008 8-channel 10-bit ADC [part_number=MCP3008]
  S1 = Round Pushbutton
  S2 = Round Pushbutton
  S3 = Round Pushbutton

nets:
  3V3: Raspberry_Pi_1.3v3, Part1.VCC, IC1.no_name_yet#15, IC1.no_name_yet#16
  N1: Raspberry_Pi_1.GPIO17, S3.leg0
  N2: Raspberry_Pi_1.GPIO10, IC1.no_name_yet#11
  N3: Raspberry_Pi_1.GPIO9, IC1.no_name_yet#12
  N4: Raspberry_Pi_1.GPIO11, IC1.no_name_yet#13
  N5: Raspberry_Pi_1.GPIO8, IC1.no_name_yet#10
  N6: Raspberry_Pi_1.GPIO24, S1.leg0
  N7: Raspberry_Pi_1.GPIO23, S2.leg0
  GND: Raspberry_Pi_1.GND, Part1.GND, IC1.no_name_yet#9, IC1.no_name_yet#14, S1.leg1, S2.leg1, S3.leg1
  N8: Part1.HORZ, IC1.no_name_yet#1
  N9: Part1.VERT, IC1.no_name_yet#2

custom parts:
  Raspberry Pi 4: The RPi4, a faster version of the awesome Raspberry Pi 2 B ARM Board with 40 pin gpio. Ready for special Raspberry Pi B+ and RPi2 Hat (Hardware attached (on) top)
